# Fritzing sketch Door Pi (saved by Fritzing 0.9.4)
circuit board: 8.53488cm x 5.63626cm
breadboards: 1

parts:
  J6 = Camdenboss CTB0158-8 [part_number=CTB0158-8 package=THT]
  12V = 2.1mm DC Barrel Jack
  DoorBell = Camdenboss CTB0158-2 [part_number=CTB0158-2 package=THT]
  DoorStrike = Camdenboss CTB0158-2 [part_number=CTB0158-2 package=THT]
  5V_LED = LEDs [package=led10mm]
  3_3V_LED = LEDs [package=led10mm]
  12V_LED = LEDs [package=led10mm]
  R1 = Resistor [tolerance=±5% resistance=220 package=THT]
  J10 = Raspberry Pi Header 40pin [package=THT]
  U2 = AQT212GH [package="DIP (Dual Inline) [THT]"]  # not connected
  U3 = AQT212GH [package="DIP (Dual Inline) [THT]"]
  U4 = AQT212GH [package="DIP (Dual Inline) [THT]"]  # not connected
  Led1 = l710a8ge dual led [package=THT]  # not connected
  Led2 = l710a8ge dual led [package=THT]  # not connected
  Led3 = l710a8ge dual led [package=THT]  # not connected
  U5 = TSR2 Series
  LLC1 = Logic Level Converter [package="Breakout board"]

nets:
  N1: J6.pin1, 12V.center_(V+), 12V_LED.A, U5.IN
  GND: J6.pin2, 12V.GND, DoorBell.pin1, DoorStrike.pin1, 5V_LED.C, 12V_LED.C, J10.GND, U3.pin3, U5.GND, LLC1.L-GND, LLC1.H-GND
  N2: J6.pin3, LLC1.HV1
  N3: J6.pin4, LLC1.HV2
  N4: J6.pin5, R1.Pin_1
  N5: 5V_LED.A, J10.5V, U5.OUT, LLC1.HV
  N6: 3_3V_LED.A, J10.3V3, LLC1.LV
  N7: R1.Pin_0, J10.IO5
  N8: J10.IO4, U3.pin2
  N9: J10.IO14, LLC1.LV1
  N10: J10.IO15, LLC1.LV2

custom parts:
  2.1mm DC Barrel Jack: 2.1mm DC Barrel Jack with Thru-Hole Connectors (breadboardable)
  Raspberry Pi Header 40pin: Raspberry Pi 40 pin header - for creating your own shields. (Mar 2020, bb: make breadboard friendly (.4in pin spacing) and add labels. Schematic add labels. PCB make oblong pins to allow routing traces between the pins.)
  AQT212GH: PhotoMOS GU 1 Form A High Capacity opto isolator. 4-pin high capacity of 1.1A, I/O isolation voltage of 5,000V
  l710a8ge dual led: KingBright L-710A8GE/11GD-RV T-1 (3mm) BI-LEVEL LED INDICATOR red/green.
  TSR2 Series: Mini DC/DC Step-Down (Buck) Converter - 5V @ 1A output - TSR12450
  Logic Level Converter: 5V to/from 3.3V logic level converter
